# Fritzing sketch PrototipoFisico (saved by Fritzing 0.9.3b)
breadboards: 1

parts:
  U2 = NodeMCU V3.0
  J1 = Basic Servo
  J2 = Piezo Speaker
  J3 = Basic Servo
  J4 = Basic Force Sensing Resistor (FSR) [package=THT]
  R1 = Resistor [tolerance=±5% resistance=220 package=THT]
  J5 = Infrared Proximity Sensor

nets:
  N1: U2.D0, J3.pulse
  N2: U2.D1, J1.pulse
  N3: U2.D2, J2.pin2
  GND: U2.GND#6, U2.GND#13, U2.GND#16, U2.GND#33, J1.gnd, J2.pin1, J3.gnd
  VCC: U2.Vin, J1.vcc, J3.vcc
  N4: U2.A0, J4.pin_1, R1.Pin_0
  N5: J4.pin_0, J5.Vcc
  N6: R1.Pin_1, J5.GND

custom parts:
  NodeMCU V3.0: ESP8266 based NodeMCU
