# Fritzing sketch PrototipoFisico (saved by Fritzing 0.9.3b)
breadboards: 1

parts:
  J1 = Basic Servo
  J2 = Piezo Speaker
  J5 = Infrared Proximity Sensor
  Q1 = NPN-Transistor [package="SOT-23 [SMD]"]
  R2 = Resistor [tolerance=±5% resistance=1k package="2010 [SMD]"]
  U3 = DC-DC_CONVERTER [package=dc-dc_converter]
  M1 = DC Motor
  U4 = NodeMCU V1.0
  S1 = Load Sensor - 50kg [part_number=SEN-10245]
  Componente1 = HX711 Weighing Sensor Module
  R3 = Resistor [tolerance=±5% resistance=1k package="0603 [SMD]"]
  R4 = Resistor [tolerance=±5% resistance=1k package="0603 [SMD]"]
  Componente2 = HX711 Weighing Sensor Module
  R5 = Resistor [tolerance=±5% resistance=1k package="0603 [SMD]"]
  R6 = Resistor [tolerance=±5% resistance=1k package="0603 [SMD]"]
  S2 = Load Sensor - 50kg [part_number=SEN-10245]

nets:
  GND: J1.gnd, J5.GND, Q1.1, U3.GND1, U3.GND2, U4.GND, Componente1.GND
  VCC: J1.vcc, J5.Vcc, U3.VIN, U4.Vin
  N1: J1.pulse, U4.D1
  N2: J2.pin2, U4.D2
  N3: J5.Vout, U4.D3
  N4: Q1.2, R2.Pin_0
  N5: Q1.0, M1.pin_2
  N6: R2.Pin_1, U4.D0
  N7: U3.VOUT, M1.pin_1, Componente1.VCC
  N8: U4.D7, Componente1.CK/TX
  N9: U4.D8, Componente1.DO/RX
  N10: S1.B, Componente1.E-
  N11: S1.W, Componente1.E+
  N12: S1.R, Componente1.A-
  N13: Componente1.A+, R3.Pin_1, R4.Pin_1
  N14: Componente2.E+, S2.W
  N15: Componente2.E-, S2.B
  N16: Componente2.A+, R5.Pin_1, R6.Pin_1
  N17: Componente2.A-, R5.Pin_0, S2.R

notes:
  Esto simula un conversor de 3v a 5v bidireccional

custom parts:
  NodeMCU V1.0: ESP8266 based NodeMCU
  Load Sensor - 50kg: Half-wheatstone bridge Load Cell modified from the Fritzing Repo This load sensor, sometimes called a strain gauge, is the same one found in digital bathroom scales (you know, the ones you use in January for your New Year's resolutions, and then forget about a month later). This sensor can measure up to about 110 pounds.
  HX711 Weighing Sensor Module: HX711 is a precision 24-bit analog-to-digital converter (ADC) designed for weigh scales and industrial control applications to interface directly with a bridge sensor.
